# Fritzing sketch schematic (saved by Fritzing 0.9.2b)

parts:
  U1 = 555 Timer [package="DIP8 [THT]"]
  R1 = Resistor [tolerance=±5% resistance=2.2M package=THT]
  R2 = Resistor [tolerance=±5% resistance=10k package=THT]
  C1 = Electrolytic Capacitor [capacitance=470µF package="100 mil [THT, electrolytic]"]
  C2 = Ceramic Capacitor [capacitance=10nF package="100 mil [THT, multilayer]"]
  U2 = Vibration Motor- ROB-08449 [package=vibe-motor-10mm]
  PNP1 = PNP-Transistor [package="TO92 [THT]"]
  D1 = Schottky Diode [part_number=1N5819 package="300 mil [THT]"]
  BAT1 = Battery Holders [package=battcom_20mm_pth]

nets:
  GND: U1.Ground, C1.-, C2.0, U2.-, D1.anode, BAT1.-
  N1: U1.Trigger, U1.Threshold, R2.Pin_0, C1.+
  N2: U1.Output, PNP1.B
  3V: U1.Reset, U1.Vcc_Supply_Voltage, R1.Pin_0, PNP1.E, BAT1.+
  N3: U1.Control_Voltage, C2.1
  N4: U1.Discharge, R1.Pin_1, R2.Pin_1
  N5: U2.+, PNP1.C, D1.cathode
